# Fritzing sketch Liftsensor ADXL335 (saved by Fritzing 0.9.3b)
breadboards: 1

parts:
  Part1 = Triple Axis Accelerometer Breakout - ADXL335
  R1 = Resistor [tolerance=±5% resistance=220 package=THT]  # not connected
  Q1 = Basic FET N-Channel [package="TO220 [THT]"]
  Part2 = Photon
  R3 = Resistor [tolerance=±5% resistance=22k package=THT]
  R4 = Resistor [tolerance=±5% resistance=33k package=THT]

nets:
  N1: Part1.XOUT, Q1.gate
  GND: Part1.GND, Part2.GND, R4.Pin_0
  VCC: Part1.VCC, Part2.3V3, R3.Pin_1
  N2: Q1.drain, R3.Pin_0
  N3: Q1.source, Part2.D0
